# Fritzing sketch smart_gate_schematics (saved by Fritzing 0.9.4)
stripboards: 1

parts:
  Part2 = Arduino Uno (Rev3)
  Raspberry_Pi1 = Raspberry Pi B rev2
  Relay1 = CAR RELAY [part_number=24V package=THT]
  U4 = RELAY-SOLIDSTATE [package=relay-s108t02]
  Relay2 = CAR RELAY [part_number=24V package=THT]
  U5 = RELAY-SOLIDSTATE [package=relay-s108t02]
  M1 = DC Motor [part_number="24V Gate Motor"]
  R_shunt = Resistor [tolerance=±5% resistance=0.01 power=3W package=THT]
  F1 = FUSE [part_number=20A package=fuse_5mm]
  F2 = FUSE [part_number=100mA package=fuse_5mm]
  S3 = Round Pushbutton
  R1 = Resistor [tolerance=±5% resistance=10k package=THT]
  R2 = Resistor [tolerance=±5% resistance=1k package=THT]
  S1 = Round Pushbutton
  S2 = Round Pushbutton
  U6 = RF-LINK_RX [package=rf-link_rx]
  ANT1 = Antenna

nets:
  N1: Part2.A0, Relay1.87A, Relay2.87A, R_shunt.Pin_1
  N2: Part2.D11_PWM/MOSI, U6.DATA
  GND: Part2.GND, Raspberry_Pi1.GND, U4.T1, U5.T1, R_shunt.Pin_0, S3.leg0, R2.Pin_1, S1.leg0, S2.leg0, U6.GND
  N3: Part2.AREF, Part2.3V3
  N4: Part2.A5/SCL, R1.Pin_1, R2.Pin_0
  5V: Part2.5V, Raspberry_Pi1.5V, U6.+5V
  N5: Raspberry_Pi1.3V3, U4.+, U5.+
  N6: Raspberry_Pi1.GPIO_23, U4.-
  N7: Raspberry_Pi1.GPIO_17, S1.leg1
  N8: Raspberry_Pi1.GPIO_27, S3.leg1
  N9: Raspberry_Pi1.GPIO_22, S2.leg1
  N10: Raspberry_Pi1.GPIO_24, U5.-
  N11: Relay1.85, Relay1.87, Relay2.85, Relay2.87, F1.2
  N12: Relay1.30, M1.pin_2
  N13: Relay1.86, U4.T2
  N14: Relay2.30, M1.pin_1
  N15: Relay2.86, U5.T2
  24V: F1.1, F2.2
  N16: F2.1, R1.Pin_0
  N17: U6.ANT, ANT1.antenna_lead

notes:
  3.3-5V Opto-coupler, SSRelay or similair,
  to drive the 24V relays with the RPi
  smart-gate, Wiring of RPi and Arduino to a 24V motorised gate, 0.1
  Optional 433MHz RX
  Arduino USB cable is connected to a USB port on the RPi, providing power and serial communication between the two
